// Logisim project 1.circ as structural Verilog: 2 circuits, main circuit main
module main (
  input  x1,
  input  x2,
  input  x3,
  output out_4,
  output out_5
);

  wire and_1_out, and_2_out, and_3_out, and_4_out, and_5_out, and_6_out, and_7_out, not_1_out, not_2_out,
       not_3_out, not_4_out, not_5_out, not_6_out;

  not not_1 (not_1_out, x1);
  not not_2 (not_2_out, x2);
  not not_3 (not_3_out, x1);
  not not_4 (not_4_out, x3);
  not not_5 (not_5_out, x2);
  not not_6 (not_6_out, x3);
  and and_1 (and_1_out, not_1_out, not_2_out, x3);
  and and_2 (and_2_out, not_3_out, x2, not_4_out);
  and and_3 (and_3_out, x1, not_5_out, not_6_out);
  and and_4 (and_4_out, x1, x2, x3);
  and and_5 (and_5_out, x1, x2);
  and and_6 (and_6_out, x2, x3);
  and and_7 (and_7_out, x1, x3);
  or or_1 (out_4, and_1_out, and_2_out, and_3_out, and_4_out);
  or or_2 (out_5, and_5_out, and_6_out, and_7_out);
endmodule

module _8_bit (
  input  in_1,
  input  in_2,
  input  in_3,
  input  in_4,
  input  in_5,
  input  in_6,
  input  in_7,
  input  in_8,
  input  in_9,
  input  in_10,
  input  in_11,
  input  in_12,
  input  in_13,
  input  in_14,
  input  in_15,
  input  in_16,
  input  in_17,
  output out_18,
  output out_19,
  output out_20,
  output out_21,
  output out_22,
  output out_23,
  output out_24,
  output out_25,
  output out_26
);

  wire main_1_out_5, main_2_out_5, main_3_out_5, main_4_out_5, main_5_out_5, main_6_out_5, main_7_out_5;

  main main_1 (.x1(in_3), .x2(in_2), .x3(in_1), .out_4(out_26), .out_5(main_1_out_5));
  main main_2 (.x1(in_4), .x2(in_5), .x3(main_1_out_5), .out_4(out_25), .out_5(main_2_out_5));
  main main_3 (.x1(in_6), .x2(in_7), .x3(main_2_out_5), .out_4(out_24), .out_5(main_3_out_5));
  main main_4 (.x1(in_8), .x2(in_9), .x3(main_3_out_5), .out_4(out_23), .out_5(main_4_out_5));
  main main_5 (.x1(in_10), .x2(in_11), .x3(main_4_out_5), .out_4(out_22), .out_5(main_5_out_5));
  main main_6 (.x1(in_12), .x2(in_13), .x3(main_5_out_5), .out_4(out_21), .out_5(main_6_out_5));
  main main_7 (.x1(in_14), .x2(in_15), .x3(main_6_out_5), .out_4(out_20), .out_5(main_7_out_5));
  main main_8 (.x1(in_16), .x2(in_17), .x3(main_7_out_5), .out_4(out_19), .out_5(out_18));

  // Notes on the sheet:
  //   слева направо
  //   справа налево
endmodule
