// Logisim project 3.circ as structural Verilog: 1 circuit, main circuit main
module main (
  output out_1,
  output out_2,
  output out_3
);

  wire clock_1_out, nand_1_out, nand_2_out, or_1_out;

  Clock clock_1 (.out(clock_1_out));
  T_Flip_Flop t_ff_1 (.clk(clock_1_out), .T(1'b1), .Q(out_3));  // open: Qn, preset, reset, en
  nand nand_1 (nand_1_out, out_3, out_3);
  T_Flip_Flop t_ff_2 (.clk(clock_1_out), .T(nand_1_out), .Q(out_2));  // open: Qn, preset, reset, en
  or or_1 (or_1_out, out_3, out_2);
  nand nand_2 (nand_2_out, or_1_out, or_1_out);
  T_Flip_Flop t_ff_3 (.clk(clock_1_out), .T(nand_2_out), .Q(out_1));  // open: Qn, preset, reset, en
endmodule
